// Logisim project nhi.circ as structural Verilog: 1 circuit, main circuit main
module main (
  input  x,
  input  PRE,
  input  CLR,
  output z
);

  wire and_1_out, clock_1_out, d_ff_1_q, d_ff_1_qn, j_k_ff_1_q, j_k_ff_1_qn, not_1_out, not_2_out;

  Clock clock_1 (.out(clock_1_out));
  not not_1 (not_1_out, PRE);
  not not_2 (not_2_out, CLR);
  and and_1 (and_1_out, x, j_k_ff_1_q);
  D_Flip_Flop #(.trigger("falling")) d_ff_1 (
    .clk(clock_1_out), .D(and_1_out), .Q(d_ff_1_q), .Qn(d_ff_1_qn), .preset(not_1_out), .reset(not_2_out));  // open: en
  J_K_Flip_Flop #(.trigger("falling")) j_k_ff_1 (
    .J(d_ff_1_qn), .clk(clock_1_out), .K(d_ff_1_q), .Q(j_k_ff_1_q), .Qn(j_k_ff_1_qn), .preset(not_1_out),
    .reset(not_2_out));  // open: en
  or or_1 (z, d_ff_1_qn, j_k_ff_1_qn);

  // Notes on the sheet:
  //   CLK
endmodule
