// Logisim project in4out4.circ as structural Verilog: 1 circuit, main circuit main
module main (
  input  a0,
  input  a1,
  input  a2,
  input  a3,
  output out_5,
  output out_6,
  output out_7,
  output out_8
);

  wire and_1_out, and_2_out, and_3_out, and_4_out, not_1_out, not_2_out, not_3_out, not_4_out;

  not not_1 (not_1_out, a0);
  not not_2 (not_2_out, a1);
  not not_3 (not_3_out, a2);
  not not_4 (not_4_out, a3);
  and and_1 (and_1_out, not_2_out, a0, not_3_out, not_4_out);
  and and_2 (and_2_out, not_1_out, not_3_out, a1, not_4_out);
  and and_3 (and_3_out, a2, not_2_out, not_1_out, not_4_out);
  and and_4 (and_4_out, not_2_out, a3, not_3_out, not_1_out);
  NotExactlyOne xnor_1 (.out(out_5), .in0(a0), .in1(a1), .in3(a2), .in4(a3));
  or or_1 (out_6, and_1_out, and_2_out, and_3_out, and_4_out);
  and and_5 (out_7, not_2_out, not_3_out, not_1_out, not_4_out);
  and and_6 (out_8, a3, a2, a1, a0);
endmodule
