// Logisim project simpl.circ as structural Verilog: 2 circuits, main circuit main
module main (
  input  in_1,
  input  in_2,
  input  in_3,
  input  in_4,
  output out_5,
  output out_6,
  output out_7,
  output out_8
);

  wire and_1_out, and_2_out, and_3_out, and_4_out, not_1_out, not_2_out, not_3_out, not_4_out;

  not not_1 (not_1_out, in_1);
  not not_2 (not_2_out, in_2);
  not not_3 (not_3_out, in_3);
  not not_4 (not_4_out, in_4);
  and and_1 (and_1_out, in_1, not_2_out, not_3_out, not_4_out);
  and and_2 (and_2_out, in_2, not_1_out, not_3_out, not_4_out);
  and and_3 (and_3_out, in_3, not_1_out, not_2_out, not_4_out);
  and and_4 (and_4_out, not_1_out, not_2_out, not_3_out, in_4);
  nor nor_1 (out_5, not_1_out, not_2_out, not_3_out, not_4_out);
  and and_5 (out_6, not_1_out, not_2_out, not_3_out, not_4_out);
  and and_6 (out_7, in_1, in_2, in_3, in_4);
  or or_1 (out_8, and_1_out, and_2_out, and_3_out, and_4_out);
endmodule

module mainn (
  input  in0,
  input  in1,
  input  in2,
  input  in3,
  output out_5,
  output out_6,
  output out_7,
  output out_8,
  output out_9,
  output out_10,
  output out_11
);

  wire B_nC_out, B_nCD_out, B_nD_out, BD_out, C_nD_out, CD_out, nB_nD_out, nBC_out, nC_nD_out, not_1_out,
       not_2_out;

  not not_1 (not_1_out, in1);
  not not_2 (not_2_out, in2);
  not not_3 (not_1_out, in3);
  and BD (BD_out, in1, in3);
  and nB_nD (nB_nD_out, not_1_out, not_1_out);
  and nC_nD (nC_nD_out, not_2_out, not_1_out);
  and CD (CD_out, in2, in3);
  and C_nD (C_nD_out, in2, not_1_out);
  and nBC (nBC_out, not_1_out, in2);
  and B_nCD (B_nCD_out, not_1_out, in2, in3);
  and B_nC (B_nC_out, not_1_out, in2);
  and B_nD (B_nD_out, not_1_out, in1);
  or a (out_5, in0, BD_out, in2);
  or b (out_6, not_1_out, nC_nD_out, CD_out);
  or c (out_7, in1, not_2_out, in3);
  or e (out_8, nB_nD_out, C_nD_out);
  or d (out_9, C_nD_out, nB_nD_out, nBC_out, B_nCD_out, in0);
  or f (out_10, in0, nC_nD_out, B_nC_out, B_nD_out);
  or g (out_11, in0, B_nC_out, C_nD_out, nBC_out);
endmodule
